# Fritzing sketch SunrisePCB-Teensy (saved by Fritzing 0.9.3b)
perfboards: 1

parts:
  To_LEDs = Power plug
  IRF530 = Basic FET N-Channel [package="TO220 [THT]"]
  Part1 = Adafruit DS3231 [part_number="DS3231 RTC"]
  7-Segment = female pin header, 4 pins [form="♀ (female)"]
  R3 = Resistor [tolerance=±5% resistance=10k package=THT]
  12_VDC = Power plug
  Encoder = Rotary Encoder with Knob
  Teensy_3_1 = Teensy 3.1
  U1 = Voltage Regulator - 5V [package="TO220 [THT]"]

nets:
  N1: To_LEDs.GND, IRF530.drain
  12V: To_LEDs.VCC, 12_VDC.VCC, U1.input_voltage
  N2: IRF530.gate, Teensy_3_1.D6
  GND: IRF530.source, Part1.GND, 7-Segment.pin3, R3.Pin_0, 12_VDC.GND, Encoder.no_name_yet#2, Teensy_3_1.GND, U1.GND
  3.3V: Part1.Vin, 7-Segment.pin4, Teensy_3_1.3V3
  N3: Part1.SCL, 7-Segment.pin2, Teensy_3_1.A5/D19
  N4: Part1.SDA, 7-Segment.pin1, Teensy_3_1.A4/D18
  N5: R3.Pin_1, Encoder.no_name_yet#5
  N6: Encoder.no_name_yet#1, Teensy_3_1.A1/D15
  N7: Encoder.no_name_yet#3, Teensy_3_1.A2/D16
  N8: Encoder.no_name_yet#4, Teensy_3_1.D12
  N9: Teensy_3_1.Vin, U1.output_voltage

notes:
  - - +
  + - -
  12VDC Input
  Output to LEDs

custom parts:
  Adafruit DS3231: The datasheet for the DS3231 explains that this part is an "Extremely Accurate I²C-Integrated RTC/TCXO/Crystal". And, hey, it does exactly what it says on the tin! This Real Time Clock (RTC) is the most precise you can get in a small, low power package. Most RTCs use an external 32kHz timing crystal that is used to keep time with low current draw. And that's all well and good, but those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
  Rotary Encoder with Knob: Rotary Encoder with 1/4" Shaft and Knob
