# Fritzing sketch SunrisePCBMega (saved by Fritzing 0.9.3b)

parts:
  To_LEDs = Power plug
  IRF530 = Basic FET N-Channel [package="TO220 [THT]"]
  Part1 = Adafruit DS3231 [part_number="DS3231 RTC"]
  7-Segment = female pin header, 4 pins [form="♀ (female)"]
  R3 = Resistor [tolerance=±5% resistance=10k package=THT]
  12_VDC = Power plug
  Part2 = Arduino Mega Proto Shield (v6)
  Encoder = Rotary Encoder with Knob

nets:
  N1: To_LEDs.GND, IRF530.drain, Part2.N$168
  12V: To_LEDs.VCC, 12_VDC.VCC, Part2.+9V
  N2: IRF530.gate, Part2.D12, Part2.N$156
  GND: IRF530.source, Part1.GND, 7-Segment.pin3, R3.Pin_0, 12_VDC.GND, Part2.GND, Part2.N$180, Part2.N$312, Part2.N$333, Part2.N$337, Part2.N$359, Encoder.no_name_yet#2
  3.3V: Part1.Vin, 7-Segment.pin4, Part2.+3V3, Part2.N$348, Part2.N$350
  N3: Part1.SCL, 7-Segment.pin2, Part2.SCL, Part2.N$270, Part2.N$288
  N4: Part1.SDA, 7-Segment.pin1, Part2.SDA, Part2.N$250, Part2.N$254
  N5: Part1.BAT, Part2.N$215
  N6: Part1.32KHZ, Part2.N$204
  N7: Part1.SQW, Part2.N$105
  N8: R3.Pin_1, Part2.N$282, Encoder.no_name_yet#5
  N9: Part2.D7, Part2.N$313, Encoder.no_name_yet#1
  N10: Part2.D8, Part2.N$241, Encoder.no_name_yet#3
  N11: Part2.RX1, Part2.N$296, Encoder.no_name_yet#4

notes:
  - - +
  + - -
  12VDC Input
  Output to LEDs

custom parts:
  Adafruit DS3231: The datasheet for the DS3231 explains that this part is an "Extremely Accurate I²C-Integrated RTC/TCXO/Crystal". And, hey, it does exactly what it says on the tin! This Real Time Clock (RTC) is the most precise you can get in a small, low power package. Most RTCs use an external 32kHz timing crystal that is used to keep time with low current draw. And that's all well and good, but those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
  Rotary Encoder with Knob: Rotary Encoder with 1/4" Shaft and Knob
